// Digital circuit A Multiplicando varios B.dig as structural Verilog
module A_Multiplicando_varios_B (
  input  B0,
  input  B1,
  input  B2,
  input  B3,
  input  A0,
  output M0,
  output M1,
  output M2,
  output M3
);

  and and_1 (M0, A0, B0);
  and and_2 (M1, A0, B1);
  and and_3 (M2, A0, B2);
  and and_4 (M3, A0, B3);
endmodule
