// Digital circuit Circuito FINAL.dig as structural Verilog
module Circuito_FINAL (
  input  B3,
  input  B2,
  input  B1,
  input  B0,
  input  O1,
  input  A3,
  input  A2,
  input  A1,
  input  A0,
  input  O0,
  input  A4,
  input  A5,
  input  B4,
  input  B5,
  output F,
  output s7,
  output s6,
  output s5,
  output s4,
  output s3,
  output s2,
  output s1,
  output s0
);

  Circuito_Principal circuito_principal_1 (
    .B0(B0), .B1(B1), .B2(B2), .B3(B3), .B4(B4), .B5(B5), .O0(O1), .O1(O0), .A0(A0), .A1(A1), .A2(A2),
    .A3(A3), .A4(A4), .A5(A5), .s0(F), .s1(s7), .s2(s6), .s3(s5), .s4(s4), .s5(s3), .s6(s2), .s7(s1), .F(s0));
endmodule
