// Digital circuit Circuito Principal.dig as structural Verilog
module Circuito_Principal (
  input  B0,
  input  B1,
  input  B2,
  input  B3,
  input  B4,
  input  B5,
  input  O0,
  input  O1,
  input  A0,
  input  A1,
  input  A2,
  input  A3,
  input  A4,
  input  A5,
  output s0,
  output s1,
  output s2,
  output s3,
  output s4,
  output s5,
  output s6,
  output s7,
  output F
);

  wire comparador_1_f, multiplicador_1_f, multiplicador_1_s0, multiplicador_1_s1, multiplicador_1_s2,
       multiplicador_1_s3, multiplicador_1_s4, multiplicador_1_s5, multiplicador_1_s6, multiplicador_1_s7,
       somador_1_f, somador_1_s0, somador_1_s1, somador_1_s2, somador_1_s3, somador_1_s4, somador_1_s5,
       subtrator_1_f, subtrator_1_s0, subtrator_1_s1, subtrator_1_s2, subtrator_1_s3, subtrator_1_s4,
       subtrator_1_s5;

  Multiplicador multiplicador_1 (
    .B0(B0), .B1(B1), .B2(B2), .B3(B3), .B4(B4), .B5(B5), .A0(A0), .A1(A1), .A2(A2), .A3(A3), .A4(A4),
    .A5(A5), .F(multiplicador_1_f), .S0(multiplicador_1_s0), .S1(multiplicador_1_s1),
    .S2(multiplicador_1_s2), .S3(multiplicador_1_s3), .S4(multiplicador_1_s4), .S5(multiplicador_1_s5),
    .S6(multiplicador_1_s6), .S7(multiplicador_1_s7));
  Comparador comparador_1 (
    .B0(B0), .B1(B1), .B2(B2), .B3(B3), .B4(B4), .B5(B5), .A0(A0), .A1(A1), .A2(A2), .A3(A3), .A4(A4),
    .A5(A5), .F(comparador_1_f));
  Seletor_De_Operacao_de_6_bits seletor_de_operacao_de_6_bits_1 (
    .F_Som(somador_1_f), .S0_Som(somador_1_s0), .S1_Som(somador_1_s1), .S2_Som(somador_1_s2),
    .S3_Som(somador_1_s3), .S4_Som(somador_1_s4), .S5_Som(somador_1_s5), .F_Sub(subtrator_1_f),
    .S0_Sub(subtrator_1_s0), .S1_Sub(subtrator_1_s1), .S2_Sub(subtrator_1_s2), .S3_Sub(subtrator_1_s3),
    .S4_Sub(subtrator_1_s4), .S5_Sub(subtrator_1_s5), .S0_Com(comparador_1_f), .F_Mul(multiplicador_1_f),
    .S0_Mul(multiplicador_1_s0), .S1_Mul(multiplicador_1_s1), .S2_Mul(multiplicador_1_s2),
    .S3_Mul(multiplicador_1_s3), .S4_Mul(multiplicador_1_s4), .S5_Mul(multiplicador_1_s5),
    .S6_Mul(multiplicador_1_s6), .S7_Mul(multiplicador_1_s7), ._00(O0), ._01(O1), .S0(s0), .S1(s1), .S2(s2),
    .S3(s3), .S4(s4), .S5(s5), .S6(s6), .S7(s7), .F(F));
  Subtrator subtrator_1 (
    .B0(B0), .B1(B1), .B2(B2), .B3(B3), .B4(B4), .B5(B5), .A0(A0), .A1(A1), .A2(A2), .A3(A3), .A4(A4),
    .A5(A5), .S0(subtrator_1_s0), .S1(subtrator_1_s1), .S2(subtrator_1_s2), .S3(subtrator_1_s3),
    .S4(subtrator_1_s4), .S5(subtrator_1_s5), .F(subtrator_1_f));
  Somador somador_1 (
    .B0(B0), .B1(B1), .B2(B2), .B3(B3), .B4(B4), .B5(B5), .A0(A0), .A1(A1), .A2(A2), .A3(A3), .A4(A4),
    .A5(A5), .S0(somador_1_s0), .S1(somador_1_s1), .S2(somador_1_s2), .S3(somador_1_s3), .S4(somador_1_s4),
    .S5(somador_1_s5), .F(somador_1_f));
endmodule
