// Digital circuit Comparador.dig as structural Verilog
module Comparador (
  input  B0,
  input  B1,
  input  B2,
  input  B3,
  input  B4,
  input  B5,
  input  A0,
  input  A1,
  input  A2,
  input  A3,
  input  A4,
  input  A5,
  output F
);

  wire xnor_1_out, xnor_2_out, xnor_3_out, xnor_4_out, xnor_5_out, xnor_6_out;

  xnor xnor_1 (xnor_1_out, B0, A0);
  xnor xnor_2 (xnor_2_out, B1, A1);
  xnor xnor_3 (xnor_3_out, B2, A2);
  xnor xnor_4 (xnor_4_out, B3, A3);
  xnor xnor_5 (xnor_5_out, B4, A4);
  xnor xnor_6 (xnor_6_out, B5, A5);
  and and_1 (F, xnor_1_out, xnor_2_out, xnor_3_out, xnor_4_out, xnor_5_out, xnor_6_out);
endmodule
