// Digital circuit Identificador de overflow.dig as structural Verilog
module Identificador_de_overflow (
  input  A,
  input  B,
  input  S,
  output F
);

  wire and_1_out, and_2_out;

  and and_1 (and_1_out, A, ~S, B);  // And
  and and_2 (and_2_out, ~A, S, ~B);  // And
  or or_1 (F, and_1_out, and_2_out);
endmodule
