// Digital circuit Multiplicador.dig as structural Verilog
module Multiplicador (
  input  B0,
  input  B1,
  input  B2,
  input  B3,
  input  B4,
  input  B5,
  input  A0,
  input  A1,
  input  A2,
  input  A3,
  input  A4,
  input  A5,
  output F,
  output S0,
  output S1,
  output S2,
  output S3,
  output S4,
  output S5,
  output S6,
  output S7
);

  wire a_multiplicando_varios_b_1_m0, a_multiplicando_varios_b_1_m1, a_multiplicando_varios_b_1_m2,
       a_multiplicando_varios_b_1_m3, a_multiplicando_varios_b_2_m0, a_multiplicando_varios_b_2_m1,
       a_multiplicando_varios_b_2_m2, a_multiplicando_varios_b_2_m3, a_multiplicando_varios_b_3_m0,
       a_multiplicando_varios_b_3_m1, a_multiplicando_varios_b_3_m2, a_multiplicando_varios_b_3_m3,
       a_multiplicando_varios_b_4_m0, a_multiplicando_varios_b_4_m1, a_multiplicando_varios_b_4_m2,
       a_multiplicando_varios_b_4_m3, somador_dse_8_bits_1_s0, somador_dse_8_bits_1_s1,
       somador_dse_8_bits_1_s2, somador_dse_8_bits_1_s3, somador_dse_8_bits_1_s4, somador_dse_8_bits_1_s5,
       somador_dse_8_bits_1_s6, somador_dse_8_bits_2_cout, somador_dse_8_bits_2_s0, somador_dse_8_bits_2_s1,
       somador_dse_8_bits_2_s2, somador_dse_8_bits_2_s3, somador_dse_8_bits_2_s4, somador_dse_8_bits_2_s5,
       somador_dse_8_bits_2_s6;

  or or_1 (F, B5, B4, A4, A5);
  A_Multiplicando_varios_B a_multiplicando_varios_b_1 (
    .B0(B0), .B1(B1), .B2(B2), .B3(B3), .A0(A0), .M0(a_multiplicando_varios_b_1_m0),
    .M1(a_multiplicando_varios_b_1_m1), .M2(a_multiplicando_varios_b_1_m2), .M3(a_multiplicando_varios_b_1_m3));
  A_Multiplicando_varios_B a_multiplicando_varios_b_2 (
    .B0(B0), .B1(B1), .B2(B2), .B3(B3), .A0(A1), .M0(a_multiplicando_varios_b_2_m0),
    .M1(a_multiplicando_varios_b_2_m1), .M2(a_multiplicando_varios_b_2_m2), .M3(a_multiplicando_varios_b_2_m3));
  A_Multiplicando_varios_B a_multiplicando_varios_b_3 (
    .B0(B0), .B1(B1), .B2(B2), .B3(B3), .A0(A2), .M0(a_multiplicando_varios_b_3_m0),
    .M1(a_multiplicando_varios_b_3_m1), .M2(a_multiplicando_varios_b_3_m2), .M3(a_multiplicando_varios_b_3_m3));
  A_Multiplicando_varios_B a_multiplicando_varios_b_4 (
    .B0(B0), .B1(B1), .B2(B2), .B3(B3), .A0(A3), .M0(a_multiplicando_varios_b_4_m0),
    .M1(a_multiplicando_varios_b_4_m1), .M2(a_multiplicando_varios_b_4_m2), .M3(a_multiplicando_varios_b_4_m3));
  Somador_dse_8_bits somador_dse_8_bits_1 (
    .A0(1'b0), .A1(a_multiplicando_varios_b_2_m0), .A2(a_multiplicando_varios_b_2_m1),
    .A3(a_multiplicando_varios_b_2_m2), .A4(a_multiplicando_varios_b_2_m3), .A5(1'b0), .A6(1'b0), .A7(1'b0),
    .B0(a_multiplicando_varios_b_1_m0), .B1(a_multiplicando_varios_b_1_m1),
    .B2(a_multiplicando_varios_b_1_m2), .B3(a_multiplicando_varios_b_1_m3), .B4(1'b0), .B5(1'b0), .B6(1'b0),
    .B7(1'b0), .S0(somador_dse_8_bits_1_s0), .S1(somador_dse_8_bits_1_s1), .S2(somador_dse_8_bits_1_s2),
    .S3(somador_dse_8_bits_1_s3), .S4(somador_dse_8_bits_1_s4), .S5(somador_dse_8_bits_1_s5),
    .S6(somador_dse_8_bits_1_s6), .COUT(somador_dse_8_bits_1_s6));
  Somador_dse_8_bits somador_dse_8_bits_2 (
    .A0(1'b0), .A1(1'b0), .A2(1'b0), .A3(a_multiplicando_varios_b_4_m0), .A4(a_multiplicando_varios_b_4_m1),
    .A5(a_multiplicando_varios_b_4_m2), .A6(a_multiplicando_varios_b_4_m3), .A7(1'b0), .B0(1'b0), .B1(1'b0),
    .B2(a_multiplicando_varios_b_3_m0), .B3(a_multiplicando_varios_b_3_m1),
    .B4(a_multiplicando_varios_b_3_m2), .B5(a_multiplicando_varios_b_3_m3), .B6(1'b0), .B7(1'b0),
    .S0(somador_dse_8_bits_2_s0), .S1(somador_dse_8_bits_2_s1), .S2(somador_dse_8_bits_2_s2),
    .S3(somador_dse_8_bits_2_s3), .S4(somador_dse_8_bits_2_s4), .S5(somador_dse_8_bits_2_s5),
    .S6(somador_dse_8_bits_2_s6), .COUT(somador_dse_8_bits_2_cout));
  Somador_dse_8_bits somador_dse_8_bits_3 (
    .A0(somador_dse_8_bits_2_s0), .A1(somador_dse_8_bits_2_s1), .A2(somador_dse_8_bits_2_s2),
    .A3(somador_dse_8_bits_2_s3), .A4(somador_dse_8_bits_2_s4), .A5(somador_dse_8_bits_2_s5),
    .A6(somador_dse_8_bits_2_s6), .A7(somador_dse_8_bits_2_cout), .B0(somador_dse_8_bits_1_s0),
    .B1(somador_dse_8_bits_1_s1), .B2(somador_dse_8_bits_1_s2), .B3(somador_dse_8_bits_1_s3),
    .B4(somador_dse_8_bits_1_s4), .B5(somador_dse_8_bits_1_s5), .B6(somador_dse_8_bits_1_s6),
    .B7(somador_dse_8_bits_1_s6), .S0(S0), .S1(S1), .S2(S2), .S3(S3), .S4(S4), .S5(S5), .S6(S6), .COUT(S7));
endmodule
