// Digital circuit Mux Para o Overflow.dig as structural Verilog
module Mux_Para_o_Overflow (
  input  S0_soma,
  input  \SO_Subtração ,
  input  \SO_Multiplicação ,
  input  _00,
  input  _10,
  output S1
);

  wire and_1_out, and_2_out, and_3_out, or_2_out;

  and and_1 (and_1_out, S0_soma, ~_00, ~_10);  // And
  or or_1 (S1, or_2_out, and_1_out);
  and and_2 (and_2_out, \SO_Subtração , _00, ~_10);  // And
  or or_2 (or_2_out, and_3_out, and_2_out);
  and and_3 (and_3_out, \SO_Multiplicação , _00, _10);
endmodule
