// Digital circuit Mux para a multiplicacao.dig as structural Verilog
module Mux_para_a_multiplicacao (
  input  \SO_Multiplicação ,
  input  _00,
  input  _10,
  output S0
);

  and and_1 (S0, \SO_Multiplicação , _00, _10);
endmodule
