// Digital circuit Mux para as contas.dig as structural Verilog
module Mux_para_as_contas (
  input  S0_soma,
  input  \SO_Subtração ,
  input  \S0_Comparação ,
  input  \SO_Multiplicação ,
  input  _00,
  input  _01,
  output F
);

  wire and_1_out, and_2_out, and_3_out, and_4_out, not_1_out, not_2_out;

  not not_1 (not_1_out, _00);
  not not_2 (not_2_out, _01);
  and and_1 (and_1_out, not_2_out, not_1_out, S0_soma);
  and and_2 (and_2_out, _01, not_1_out, \S0_Comparação );
  and and_3 (and_3_out, not_2_out, _00, \SO_Subtração );
  and and_4 (and_4_out, _01, _00, \SO_Multiplicação );
  or or_1 (F, and_1_out, and_2_out, and_3_out, and_4_out);
endmodule
