// Digital circuit Seletor De Operacao de 6 bits.dig as structural Verilog
module Seletor_De_Operacao_de_6_bits (
  input  F_Som,
  input  S0_Som,
  input  S1_Som,
  input  S2_Som,
  input  S3_Som,
  input  S4_Som,
  input  S5_Som,
  input  F_Sub,
  input  S0_Sub,
  input  S1_Sub,
  input  S2_Sub,
  input  S3_Sub,
  input  S4_Sub,
  input  S5_Sub,
  input  S0_Com,
  input  F_Mul,
  input  S0_Mul,
  input  S1_Mul,
  input  S2_Mul,
  input  S3_Mul,
  input  S4_Mul,
  input  S5_Mul,
  input  S6_Mul,
  input  S7_Mul,
  input  _00,
  input  _01,
  output S0,
  output S1,
  output S2,
  output S3,
  output S4,
  output S5,
  output S6,
  output S7,
  output F
);

  Mux_para_as_contas mux_para_as_contas_1 (
    .S0_soma(S0_Som), .\SO_Subtração (S0_Sub), .\S0_Comparação (S0_Com), .\SO_Multiplicação (S0_Mul),
    ._00(_00), ._01(_01), .F(S0));
  Mux_para_as_contas mux_para_as_contas_2 (
    .S0_soma(S1_Som), .\SO_Subtração (S1_Sub), .\S0_Comparação (1'b0), .\SO_Multiplicação (S1_Mul),
    ._00(_00), ._01(_01), .F(S1));
  Mux_para_as_contas mux_para_as_contas_3 (
    .S0_soma(S2_Som), .\SO_Subtração (S2_Sub), .\S0_Comparação (1'b0), .\SO_Multiplicação (S2_Mul),
    ._00(_00), ._01(_01), .F(S2));
  Mux_para_as_contas mux_para_as_contas_4 (
    .S0_soma(S3_Som), .\SO_Subtração (S3_Sub), .\S0_Comparação (1'b0), .\SO_Multiplicação (S3_Mul),
    ._00(_00), ._01(_01), .F(S3));
  Mux_para_as_contas mux_para_as_contas_5 (
    .S0_soma(S4_Som), .\SO_Subtração (S4_Sub), .\S0_Comparação (1'b0), .\SO_Multiplicação (S4_Mul),
    ._00(_00), ._01(_01), .F(S4));
  Mux_para_as_contas mux_para_as_contas_6 (
    .S0_soma(S5_Som), .\SO_Subtração (S5_Sub), .\S0_Comparação (1'b0), .\SO_Multiplicação (S5_Mul),
    ._00(_00), ._01(_01), .F(S5));
  Mux_para_a_multiplicacao mux_para_a_multiplicacao_1 (.\SO_Multiplicação (S6_Mul), ._00(_00), ._10(_01), .S0(S6));
  Mux_para_a_multiplicacao mux_para_a_multiplicacao_2 (.\SO_Multiplicação (S7_Mul), ._00(_00), ._10(_01), .S0(S7));
  Mux_Para_o_Overflow mux_para_o_overflow_1 (
    .S0_soma(F_Som), .\SO_Subtração (F_Sub), .\SO_Multiplicação (F_Mul), ._00(_00), ._10(_01), .S1(F));
endmodule
