// Digital circuit Somador Do complemento de 2.dig as structural Verilog
module Somador_Do_complemento_de_2 (
  input  B0,
  input  B1,
  input  B2,
  input  B3,
  input  B4,
  input  B5,
  output S0,
  output S1,
  output S2,
  output S3,
  output S4,
  output S5
);

  wire helfl_adder_1_cout, helfl_adder_2_cout, helfl_adder_3_cout, helfl_adder_4_cout, helfl_adder_5_cout;

  Helfl_Adder helfl_adder_1 (.A(1'b1), .B(B0), .S(S0), .Cout(helfl_adder_1_cout));
  Helfl_Adder helfl_adder_2 (.A(helfl_adder_1_cout), .B(B1), .S(S1), .Cout(helfl_adder_2_cout));
  Helfl_Adder helfl_adder_3 (.A(helfl_adder_2_cout), .B(B2), .S(S2), .Cout(helfl_adder_3_cout));
  Helfl_Adder helfl_adder_4 (.A(helfl_adder_3_cout), .B(B3), .S(S3), .Cout(helfl_adder_4_cout));
  Helfl_Adder helfl_adder_5 (.A(helfl_adder_4_cout), .B(B4), .S(S4), .Cout(helfl_adder_5_cout));
  Helfl_Adder helfl_adder_6 (.A(helfl_adder_5_cout), .B(B5), .S(S5));  // open: Cout
endmodule
