// Digital circuit Somador dse 8 bits.dig as structural Verilog
module Somador_dse_8_bits (
  input  A0,
  input  A1,
  input  A2,
  input  A3,
  input  A4,
  input  A5,
  input  A6,
  input  A7,
  input  B0,
  input  B1,
  input  B2,
  input  B3,
  input  B4,
  input  B5,
  input  B6,
  input  B7,
  output S0,
  output S1,
  output S2,
  output S3,
  output S4,
  output S5,
  output S6,
  output COUT
);

  wire full_adder_1_cout, full_adder_2_cout, full_adder_3_cout, full_adder_4_cout, full_adder_5_cout,
       full_adder_6_cout, helfl_adder_1_cout;

  Helfl_Adder helfl_adder_1 (.A(A0), .B(B0), .S(S0), .Cout(helfl_adder_1_cout));
  Full_Adder full_adder_1 (.A(A1), .B(B1), .Cin(helfl_adder_1_cout), .S(S1), .Cout(full_adder_1_cout));
  Full_Adder full_adder_2 (.A(A2), .B(B2), .Cin(full_adder_1_cout), .S(S2), .Cout(full_adder_2_cout));
  Full_Adder full_adder_3 (.A(A3), .B(B3), .Cin(full_adder_2_cout), .S(S3), .Cout(full_adder_3_cout));
  Full_Adder full_adder_4 (.A(A4), .B(B4), .Cin(full_adder_3_cout), .S(S4), .Cout(full_adder_4_cout));
  Full_Adder full_adder_5 (.A(A5), .B(B5), .Cin(full_adder_4_cout), .S(S5), .Cout(full_adder_5_cout));
  Full_Adder full_adder_6 (.A(A6), .B(B6), .Cin(full_adder_5_cout), .S(S6), .Cout(full_adder_6_cout));
  Full_Adder full_adder_7 (.A(A7), .B(B7), .Cin(full_adder_6_cout), .S(COUT));  // open: Cout
endmodule
