// Digital circuit Subtrator.dig as structural Verilog
module Subtrator (
  input  B0,
  input  B1,
  input  B2,
  input  B3,
  input  B4,
  input  B5,
  input  A0,
  input  A1,
  input  A2,
  input  A3,
  input  A4,
  input  A5,
  output S0,
  output S1,
  output S2,
  output S3,
  output S4,
  output S5,
  output F
);

  wire complemento_de_2_1_s0, complemento_de_2_1_s1, complemento_de_2_1_s2, complemento_de_2_1_s3,
       complemento_de_2_1_s4, complemento_de_2_1_s5;

  Complemento_de_2 complemento_de_2_1 (
    .B0(B0), .B1(B1), .B2(B2), .B3(B3), .B4(B4), .B5(B5), .S0(complemento_de_2_1_s0),
    .S1(complemento_de_2_1_s1), .S2(complemento_de_2_1_s2), .S3(complemento_de_2_1_s3),
    .S4(complemento_de_2_1_s4), .S5(complemento_de_2_1_s5));
  Somador somador_1 (
    .B0(complemento_de_2_1_s0), .B1(complemento_de_2_1_s1), .B2(complemento_de_2_1_s2),
    .B3(complemento_de_2_1_s3), .B4(complemento_de_2_1_s4), .B5(complemento_de_2_1_s5), .A0(A0), .A1(A1),
    .A2(A2), .A3(A3), .A4(A4), .A5(A5), .S0(S0), .S1(S1), .S2(S2), .S3(S3), .S4(S4), .S5(S5), .F(F));

  // Notes on the sheet:
  //   F: Overflow Somador
endmodule
